# Fritzing sketch Hoermann-Promatic2-Steuerung (saved by Fritzing 0.9.10b)

parts:
  WeMos_D1_Mini1 = WeMos D1 Mini
  Bauteil1 = BME280 Breakout
  U2 = Sharp PC817 [package=THT]
  J2 = screw terminal, 3 pins
  M1 = RioRand LM2596
  C1 = Electrolytic Capacitor [capacitance=100µF voltage=35V package="200 mil [THT, electrolytic]"]
  S1 = SWITCH-MOMENTARY-2 [package=reed_switch_pth]
  J3 = Screw terminal - 2 pins [package=THT]
  J4 = Screw terminal - 2 pins [package=THT]

nets:
  3V3: WeMos_D1_Mini1.3V3, Bauteil1.3.3V, J4.pin1, J4.pin2
  N1: WeMos_D1_Mini1.5V, M1.Pin_3, C1.+
  N2: WeMos_D1_Mini1.D1, Bauteil1.SCK/SCL
  N3: WeMos_D1_Mini1.D2, Bauteil1.SDI/SDA
  N4: WeMos_D1_Mini1.D6, U2.Pin_1
  N5: WeMos_D1_Mini1.D7, S1.1, J3.pin2
  N6: WeMos_D1_Mini1.G, Bauteil1.GND, U2.Pin_2, M1.Pin_4, S1.2, J3.pin1
  N7: U2.Pin_4, J2.pin2
  N8: U2.Pin_3, J2.pin3, M1.Pin_2
  N9: J2.pin1, M1.Pin_1

notes:
  5 21 20
  24V Impuls 0V
